// Logisim project Event Switcher.circ as structural Verilog: 1 circuit, main circuit main
module main (
  input  K,
  input  A,
  input  B,
  output O
);

  wire and_1_out, and_2_out, not_1_out;

  not not_1 (not_1_out, K);
  and and_1 (and_1_out, not_1_out, A);
  and and_2 (and_2_out, K, B);
  or or_1 (O, and_1_out, and_2_out);

  // Notes on the sheet:
  //   Switcher
  //   It gives the final data of person or event 
endmodule
