// Logisim project Register.circ as structural Verilog: 1 circuit, main circuit main
module main (
  input  IB3,
  input  IB2,
  input  IB1,
  input  IB0,
  input  Button,
  input  Enable,
  input  Clear,
  output OB3,
  output OB2,
  output OB1,
  output OB0
);

  D_Flip_Flop #(.trigger("falling")) FF3 (
    .clk(Button), .D(IB3), .Q(OB3), .en(Enable), .reset(Clear));  // open: Qn, preset
  D_Flip_Flop #(.trigger("falling")) FF2 (
    .clk(Button), .D(IB2), .Q(OB2), .en(Enable), .reset(Clear));  // open: Qn, preset
  D_Flip_Flop #(.trigger("falling")) FF1 (
    .clk(Button), .D(IB1), .Q(OB1), .en(Enable), .reset(Clear));  // open: Qn, preset
  D_Flip_Flop #(.trigger("falling")) FF0 (
    .clk(Button), .D(IB0), .Q(OB0), .en(Enable), .reset(Clear));  // open: Qn, preset

  // Notes on the sheet:
  //   Register
  //   It is a PIPO Register which stores the count of audience
endmodule
