// Logisim project S2-T13.circ as structural Verilog: 8 circuits, main circuit main
module main (
  input  P1,
  input  P0,
  input  Switch,
  input  P1_prime,
  input  P0_prime,
  input  N1,
  input  N0,
  input  E1_prime,
  input  E0_prime,
  input  E1,
  input  E0,
  input  Enable,
  input  Enable_2,
  input  Enable_3,
  input  Enable_4,
  input  Clear,
  input  Clear_2,
  input  Clear_3,
  input  Clear_4,
  input  Max_Capacity,
  input  Max_Capacity_2,
  input  Max_Capacity_3,
  input  Max_Capacity_4,
  input  in_24,
  input  in_25,
  input  in_26,
  input  in_27,
  input  in_28,
  input  in_29,
  input  in_30,
  input  in_31,
  input  in_32,
  input  in_33,
  input  in_34,
  input  in_35,
  input  Alarm,
  input  Alarm_2,
  input  Alarm_3,
  input  Alarm_4,
  input  Enable_5,
  input  Enable_6,
  input  Enable_7,
  input  Enable_8
);

  wire A_out, and_1_out, and_2_out, and_3_out, and_4_out, and_5_out, and_6_out, and_7_out, Clock_2_out,
       Clock_3_out, Clock_4_out, Clock_out, Enter_2_out, Enter_3_out, Enter_4_out, Enter_out, ES1_o, ES2_o,
       ES3_o, ES4_o, nor_1_out, nor_2_out, not_1_out, not_2_out, not_3_out, not_4_out, not_5_out, not_6_out,
       not_7_out, not_8_out, not_9_out, not_10_out, not_11_out, not_12_out, or_1_out, or_2_out, or_3_out,
       or_4_out, or_5_out, or_6_out, or_7_out, or_8_out, s1_out, s2_out, s3_out, s4_out,
       seat_allocator_1_pc_b0, seat_allocator_1_pc_b1, seat_allocator_1_pc_b2, seat_allocator_1_pc_b3,
       seat_allocator_2_pc_b0, seat_allocator_2_pc_b1, seat_allocator_2_pc_b2, seat_allocator_2_pc_b3,
       seat_allocator_3_pc_b0, seat_allocator_3_pc_b1, seat_allocator_3_pc_b2, seat_allocator_3_pc_b3,
       seat_allocator_4_pc_b0, seat_allocator_4_pc_b1, seat_allocator_4_pc_b2, seat_allocator_4_pc_b3,
       START_2_out, START_3_out, START_4_out, START_out, time_counter_1_stop, time_counter_2_stop,
       time_counter_3_stop, time_counter_4_stop, vacancy_indicator_1_vi, vacancy_indicator_2_vi,
       vacancy_indicator_3_vi, vacancy_indicator_4_vi, xnor_1_out;
  wire [3:0] seat_allocator_1_tc_b0, seat_allocator_2_tc_b0, seat_allocator_3_tc_b0, seat_allocator_4_tc_b0;

  Button Enter (.out(Enter_out));
  Button START (.out(START_out));
  Clock Clock (.out(Clock_out));
  nor nor_1 (nor_1_out, ES1_o, ES2_o, ES3_o, ES4_o);
  or or_1 (or_1_out, Clear, Alarm);
  Time_Counter time_counter_1 (.START(START_out), .Enable(Enable_5), .Clock(Clock_out), .STOP(time_counter_1_stop));
  Event_Switcher ES1 (.K(Switch), .A(P1), .B(P1_prime), .O(ES1_o));
  Event_Switcher ES2 (.K(Switch), .A(P0), .B(P0_prime), .O(ES2_o));
  Event_Switcher ES3 (.K(Switch), .A(E1), .B(N1), .O(ES3_o));
  Event_Switcher ES4 (.K(Switch), .A(E0), .B(N0), .O(ES4_o));
  nor nor_2 (nor_2_out, ES4_o, ES3_o);
  xnor xnor_1 (xnor_1_out, ES2_o, ES1_o);
  Vacancy_Indicator vacancy_indicator_1 (
    .P1(ES1_o), .P0(ES2_o), .A3(seat_allocator_1_pc_b3), .A2(seat_allocator_1_pc_b2),
    .A1(seat_allocator_1_pc_b1), .A0(seat_allocator_1_pc_b0), .M3(Max_Capacity), .M2(in_24), .M1(in_28),
    .M0(in_32), .VI(vacancy_indicator_1_vi));  // open: Seat_Allotment__SA
  LED led_1 (.in(Alarm));
  not not_1 (not_1_out, ES2_o);
  and and_1 (and_1_out, nor_2_out, xnor_1_out);
  Seat_Allocator seat_allocator_1 (
    .TC_Button(Enter_out), .TC_Enable(Enable), .TC_Clear(Clear), .PC_Button(Enter_out), .PC_Enable(Enable),
    .PC_Clear(or_1_out), .PC_A3(1'b0), .PC_S3(1'b0), .PC_A2(1'b0), .PC_S2(1'b0), .PC_A1(1'b0), .PC_S1(1'b0),
    .PC_Ci(1'b0), .Bi(1'b0), .SA_PC_A0(nor_1_out), .SA_PC_S0(s1_out), .TC_A3(1'b0), .TC_A2(1'b0),
    .TC_A1(1'b0), .TC_Ci(1'b0), .SA_TC_A0(and_1_out), .TC_B3(seat_allocator_1_tc_b0[3]),
    .TC_B2(seat_allocator_1_tc_b0[2]), .TC_B1(seat_allocator_1_tc_b0[1]), .TC_B0(seat_allocator_1_tc_b0[0]),
    .PC_B3(seat_allocator_1_pc_b3), .PC_B2(seat_allocator_1_pc_b2), .PC_B1(seat_allocator_1_pc_b1),
    .PC_B0(seat_allocator_1_pc_b0));  // open: PC_Co, TC_Co, PC_Bo
  LED led_2 (.in(or_2_out));
  or or_2 (or_2_out, vacancy_indicator_1_vi, Alarm, time_counter_1_stop);
  not not_2 (not_2_out, ES1_o);
  not not_3 (not_3_out, ES3_o);
  Hex_Digit_Display hex_digit_display_1 (.value(seat_allocator_1_tc_b0));  // open: dp
  Button Enter_2 (.out(Enter_2_out));
  and and_2 (and_2_out, ES4_o, not_3_out, xnor_1_out);
  or or_3 (or_3_out, Clear_2, Alarm_2);
  Button START_2 (.out(START_2_out));
  Clock Clock_2 (.out(Clock_2_out));
  not not_4 (not_4_out, ES4_o);
  not not_5 (not_5_out, ES2_o);
  not not_6 (not_6_out, ES1_o);
  not not_7 (not_7_out, P1_prime);
  not not_8 (not_8_out, P0_prime);
  and and_3 (and_3_out, ES4_o, not_3_out, not_1_out, not_2_out);
  LED led_3 (.in(Alarm_2));
  Time_Counter time_counter_2 (.START(START_2_out), .Enable(Enable_6), .Clock(Clock_2_out), .STOP(time_counter_2_stop));
  not not_9 (not_9_out, E1_prime);
  not not_10 (not_10_out, E0_prime);
  Seat_Allocator seat_allocator_2 (
    .TC_Button(Enter_2_out), .TC_Enable(Enable_2), .TC_Clear(Clear_2), .PC_Button(Enter_2_out),
    .PC_Enable(Enable_2), .PC_Clear(or_3_out), .PC_A3(1'b0), .PC_S3(1'b0), .PC_A2(1'b0), .PC_S2(1'b0),
    .PC_A1(1'b0), .PC_S1(1'b0), .PC_Ci(1'b0), .Bi(1'b0), .SA_PC_A0(and_3_out), .SA_PC_S0(s2_out),
    .TC_A3(1'b0), .TC_A2(1'b0), .TC_A1(1'b0), .TC_Ci(1'b0), .SA_TC_A0(and_2_out),
    .TC_B3(seat_allocator_2_tc_b0[3]), .TC_B2(seat_allocator_2_tc_b0[2]), .TC_B1(seat_allocator_2_tc_b0[1]),
    .TC_B0(seat_allocator_2_tc_b0[0]), .PC_B3(seat_allocator_2_pc_b3), .PC_B2(seat_allocator_2_pc_b2),
    .PC_B1(seat_allocator_2_pc_b1), .PC_B0(seat_allocator_2_pc_b0));  // open: PC_Co, TC_Co, PC_Bo
  Vacancy_Indicator vacancy_indicator_2 (
    .P1(ES1_o), .P0(ES2_o), .A3(seat_allocator_2_pc_b3), .A2(seat_allocator_2_pc_b2),
    .A1(seat_allocator_2_pc_b1), .A0(seat_allocator_2_pc_b0), .M3(Max_Capacity_2), .M2(in_25), .M1(in_29),
    .M0(in_33), .VI(vacancy_indicator_2_vi));  // open: Seat_Allotment__SA
  LED led_4 (.in(or_4_out));
  or or_4 (or_4_out, vacancy_indicator_2_vi, Alarm_2, time_counter_2_stop);
  and A (A_out, not_7_out, Switch, not_8_out);
  and s1 (s1_out, A_out, not_9_out, not_10_out);
  and s2 (s2_out, A_out, not_9_out, E0_prime);
  and s3 (s3_out, A_out, not_10_out, E1_prime);
  and s4 (s4_out, A_out, E0_prime, E1_prime);
  not not_11 (not_11_out, ES2_o);
  not not_12 (not_12_out, ES1_o);
  Button Enter_3 (.out(Enter_3_out));
  Hex_Digit_Display hex_digit_display_2 (.value(seat_allocator_2_tc_b0));  // open: dp
  and and_4 (and_4_out, not_4_out, ES3_o, xnor_1_out);
  or or_5 (or_5_out, Clear_3, Alarm_3);
  Button START_3 (.out(START_3_out));
  Clock Clock_3 (.out(Clock_3_out));
  and and_5 (and_5_out, not_4_out, ES3_o, not_5_out, not_6_out);
  LED led_5 (.in(Alarm_3));
  Time_Counter time_counter_3 (.START(START_3_out), .Enable(Enable_7), .Clock(Clock_3_out), .STOP(time_counter_3_stop));
  Seat_Allocator seat_allocator_3 (
    .TC_Button(Enter_3_out), .TC_Enable(Enable_3), .TC_Clear(Clear_3), .PC_Button(Enter_3_out),
    .PC_Enable(Enable_3), .PC_Clear(or_5_out), .PC_A3(1'b0), .PC_S3(1'b0), .PC_A2(1'b0), .PC_S2(1'b0),
    .PC_A1(1'b0), .PC_S1(1'b0), .PC_Ci(1'b0), .Bi(1'b0), .SA_PC_A0(and_5_out), .SA_PC_S0(s3_out),
    .TC_A3(1'b0), .TC_A2(1'b0), .TC_A1(1'b0), .TC_Ci(1'b0), .SA_TC_A0(and_4_out),
    .TC_B3(seat_allocator_3_tc_b0[3]), .TC_B2(seat_allocator_3_tc_b0[2]), .TC_B1(seat_allocator_3_tc_b0[1]),
    .TC_B0(seat_allocator_3_tc_b0[0]), .PC_B3(seat_allocator_3_pc_b3), .PC_B2(seat_allocator_3_pc_b2),
    .PC_B1(seat_allocator_3_pc_b1), .PC_B0(seat_allocator_3_pc_b0));  // open: PC_Co, TC_Co, PC_Bo
  Vacancy_Indicator vacancy_indicator_3 (
    .P1(ES1_o), .P0(ES2_o), .A3(seat_allocator_3_pc_b3), .A2(seat_allocator_3_pc_b2),
    .A1(seat_allocator_3_pc_b1), .A0(seat_allocator_3_pc_b0), .M3(Max_Capacity_3), .M2(in_26), .M1(in_30),
    .M0(in_34), .VI(vacancy_indicator_3_vi));  // open: Seat_Allotment__SA
  LED led_6 (.in(or_6_out));
  or or_6 (or_6_out, vacancy_indicator_3_vi, Alarm_3, time_counter_3_stop);
  Hex_Digit_Display hex_digit_display_3 (.value(seat_allocator_3_tc_b0));  // open: dp
  Button Enter_4 (.out(Enter_4_out));
  and and_6 (and_6_out, ES4_o, ES3_o, xnor_1_out);
  or or_7 (or_7_out, Clear_4, Alarm_4);
  Button START_4 (.out(START_4_out));
  Clock Clock_4 (.out(Clock_4_out));
  and and_7 (and_7_out, ES4_o, ES3_o, not_11_out, not_12_out);
  LED led_7 (.in(Alarm_4));
  Time_Counter time_counter_4 (.START(START_4_out), .Enable(Enable_8), .Clock(Clock_4_out), .STOP(time_counter_4_stop));
  Seat_Allocator seat_allocator_4 (
    .TC_Button(Enter_4_out), .TC_Enable(Enable_4), .TC_Clear(Clear_4), .PC_Button(Enter_4_out),
    .PC_Enable(Enable_4), .PC_Clear(or_7_out), .PC_A3(1'b0), .PC_S3(1'b0), .PC_A2(1'b0), .PC_S2(1'b0),
    .PC_A1(1'b0), .PC_S1(1'b0), .PC_Ci(1'b0), .Bi(1'b0), .SA_PC_A0(and_7_out), .SA_PC_S0(s4_out),
    .TC_A3(1'b0), .TC_A2(1'b0), .TC_A1(1'b0), .TC_Ci(1'b0), .SA_TC_A0(and_6_out),
    .TC_B3(seat_allocator_4_tc_b0[3]), .TC_B2(seat_allocator_4_tc_b0[2]), .TC_B1(seat_allocator_4_tc_b0[1]),
    .TC_B0(seat_allocator_4_tc_b0[0]), .PC_B3(seat_allocator_4_pc_b3), .PC_B2(seat_allocator_4_pc_b2),
    .PC_B1(seat_allocator_4_pc_b1), .PC_B0(seat_allocator_4_pc_b0));  // open: PC_Co, TC_Co, PC_Bo
  Vacancy_Indicator vacancy_indicator_4 (
    .P1(ES1_o), .P0(ES2_o), .A3(seat_allocator_4_pc_b3), .A2(seat_allocator_4_pc_b2),
    .A1(seat_allocator_4_pc_b1), .A0(seat_allocator_4_pc_b0), .M3(Max_Capacity_4), .M2(in_27), .M1(in_31),
    .M0(in_35), .VI(vacancy_indicator_4_vi));  // open: Seat_Allotment__SA
  or or_8 (or_8_out, vacancy_indicator_4_vi, Alarm_4, time_counter_4_stop);
  LED led_8 (.in(or_8_out));
  Hex_Digit_Display hex_digit_display_4 (.value(seat_allocator_4_tc_b0));  // open: dp

  // Notes on the sheet:
  //   Emergency Alarm
  //   P1F
  //   P0F
  //   E1F
  //   E0F
  //   Vacancy Indicator
  //   EA_LED
  //   EAI
  //   Time Counter
  //   Event Switcher
  //   PC1
  //   S1
  //   Event-1
  //   Seat Allocator
  //   VI
  //   TCI
  //   Main Person
  //   Type
  //   TC1
  //   LED
  //   Participant Count
  //   Switch Person
  //   Type
  //   Switching Details 
  //   New Event
  //   Type
  //   Old Event
  //   Type
  //   Emergency Alarm
  //   Main Event
  //   Type
  //   PC2
  //   Vacancy Indicator
  //   EA_LED
  //   Time Counter
  //   S2
  //   Event-2
  //   Seat Allocator
  //   VI
  //   EAI
  //   TCI
  //   TC2
  //   LED
  //   w
  //   S1
  //   S2
  //   S3
  //   S4
  //   Participant Count
  //   Vacancy Indicator
  //   Emergency Alarm
  //   PC3
  //   Event-3
  //   Seat Allocator
  //   EA_LED
  //   EAI
  //   TCI
  //   Time Counter
  //   S3
  //   TC3
  //   VI
  //   State Machine For Live Event Navigator
  //   LED
  //   Participant Count
  //   Emergency Alarm
  //   Vacancy Indicator
  //   EA_LED
  //   Time Counter
  //   S4
  //   PC4
  //   Event-4
  //   Seat Allocator
  //   VI
  //   EAI
  //   TCI
  //   TC4
  //   LED
  //   Participant Count
  //   Instructions : 
  //   Team ID : S2-T13 
  //   2 . D. Sai Chaitanya, 231CS220
  //   1 . Bade V N R Mahi Tejesh Reddy, 231CS216 
  //   3 . Lava Kumar Tentu , 231CS230
  //   2. Assign max. capacity to each event.
  //   1. Set the button 'Enable' of each event and time counter to 1. 
  //   4. Give the "Main Person" and "Main Event" type input. 
  //   5. Click on the "Enter" button of respective event to enter into it.
  //   3. Click on the button "START" of Time Counter and set Clock to Tick Enabled.
  //   6. The total "Participant Count" will be displayed on Hex Digit Display. 
  //   7. Give the corresponding switching details if you want to switch the event.
endmodule

module Vacancy_Indicator (
  input  P1,
  input  P0,
  input  A3,
  input  A2,
  input  A1,
  input  A0,
  input  M3,
  input  M2,
  input  M1,
  input  M0,
  output Seat_Allotment__SA,
  output VI
);

  wire O_out, X1_out, X2_out, X3_out, X4_out;

  or O (O_out, P1, P0);
  xnor X1 (X1_out, A3, M3);
  xnor X2 (X2_out, A2, M2);
  xnor X3 (X3_out, A1, M1);
  xnor X4 (X4_out, A0, M0);
  and A (VI, X1_out, X2_out, X3_out, X4_out);
  nor N (Seat_Allotment__SA, O_out, VI);

  // Notes on the sheet:
  //   Person Type
  //   Allocated Seats
  //   Maximum Capacity
  //   VACANCY INDICATOR
  //   p
  //   w3
  //   w2
  //   w1
  //   w0
  //   It indicates the availability of seats 
  //   a
endmodule

module Time_Counter (
  input  START,
  input  Enable,
  input  Clock,
  output STOP
);

  wire FF0_q, FF0_qn, FF1_q, FF1_qn, FF2_q, FF2_qn, FF3_q, or_1_out;

  or or_1 (or_1_out, Clock, STOP);
  J_K_Flip_Flop #(.trigger("falling")) FF0 (
    .J(Enable), .clk(or_1_out), .K(Enable), .Q(FF0_q), .Qn(FF0_qn), .preset(START));  // open: en, reset
  J_K_Flip_Flop #(.trigger("falling")) FF1 (
    .J(Enable), .clk(FF0_qn), .K(Enable), .Q(FF1_q), .Qn(FF1_qn), .preset(START));  // open: en, reset
  J_K_Flip_Flop #(.trigger("falling")) FF2 (
    .J(Enable), .clk(FF1_qn), .K(Enable), .Q(FF2_q), .Qn(FF2_qn), .preset(START));  // open: en, reset
  J_K_Flip_Flop #(.trigger("falling")) FF3 (
    .J(Enable), .clk(FF2_qn), .K(Enable), .Q(FF3_q), .preset(START));  // open: Qn, en, reset
  nor nor_1 (STOP, FF3_q, FF2_q, FF1_q, FF0_q);

  // Notes on the sheet:
  //   Time Counter
  //   It indicates the remaining time of an ongoing event
endmodule

module Full_Adder (
  input  A,
  input  B,
  input  Ci,
  output S,
  output Co
);

  wire and_1_out, and_2_out, xor_1_out;

  xor xor_1 (xor_1_out, A, B);
  and and_1 (and_1_out, A, B);
  xor xor_2 (S, xor_1_out, Ci);
  and and_2 (and_2_out, xor_1_out, Ci);
  or or_1 (Co, and_2_out, and_1_out);

  // Notes on the sheet:
  //   Full Adder
endmodule

module Full_Subtractor (
  input  A,
  input  B,
  input  Bi,
  output D,
  output Bo
);

  wire and_1_out, and_2_out, not_1_out, not_2_out, xor_1_out;

  not not_1 (not_1_out, A);
  xor xor_1 (xor_1_out, A, B);
  and and_1 (and_1_out, not_1_out, B);
  not not_2 (not_2_out, xor_1_out);
  xor xor_2 (D, xor_1_out, Bi);
  and and_2 (and_2_out, not_2_out, Bi);
  or or_1 (Bo, and_2_out, and_1_out);

  // Notes on the sheet:
  //   Full Subtractor
endmodule

module Register (
  input  IB3,
  input  IB2,
  input  IB1,
  input  IB0,
  input  Button,
  input  Enable,
  input  Clear,
  output OB3,
  output OB2,
  output OB1,
  output OB0
);

  D_Flip_Flop #(.trigger("falling")) FF3 (
    .clk(Button), .D(IB3), .Q(OB3), .en(Enable), .reset(Clear));  // open: Qn, preset
  D_Flip_Flop #(.trigger("falling")) FF2 (
    .clk(Button), .D(IB2), .Q(OB2), .en(Enable), .reset(Clear));  // open: Qn, preset
  D_Flip_Flop #(.trigger("falling")) FF1 (
    .clk(Button), .D(IB1), .Q(OB1), .en(Enable), .reset(Clear));  // open: Qn, preset
  D_Flip_Flop #(.trigger("falling")) FF0 (
    .clk(Button), .D(IB0), .Q(OB0), .en(Enable), .reset(Clear));  // open: Qn, preset

  // Notes on the sheet:
  //   Register
  //   It is a PIPO Register which stores the count of audience
endmodule

module Seat_Allocator (
  input  SA_PC_A0,
  input  SA_TC_A0,
  input  PC_A3,
  input  PC_A2,
  input  PC_A1,
  input  PC_Ci,
  input  TC_A3,
  input  TC_A2,
  input  TC_A1,
  input  TC_Ci,
  input  TC_Button,
  input  TC_Enable,
  input  TC_Clear,
  input  PC_Button,
  input  PC_Enable,
  input  PC_Clear,
  input  SA_PC_S0,
  input  PC_S3,
  input  PC_S2,
  input  PC_S1,
  input  Bi,
  output PC_Co,
  output TC_Co,
  output TC_B3,
  output TC_B2,
  output TC_B1,
  output TC_B0,
  output PC_B3,
  output PC_B2,
  output PC_B1,
  output PC_Bo,
  output PC_B0
);

  wire and_1_out, and_2_out, and_3_out, and_4_out, and_5_out, and_6_out, and_7_out, and_8_out, and_9_out,
       and_10_out, and_11_out, and_12_out, full_adder_1_s, full_adder_2_co, full_adder_2_s, full_adder_3_co,
       full_adder_3_s, full_adder_4_co, full_adder_4_s, full_adder_5_s, full_adder_6_co, full_adder_6_s,
       full_adder_7_co, full_adder_7_s, full_adder_8_co, full_adder_8_s, full_subtractor_1_d,
       full_subtractor_2_bo, full_subtractor_2_d, full_subtractor_3_bo, full_subtractor_3_d,
       full_subtractor_4_bo, full_subtractor_4_d, nor_1_out, or_1_out, or_2_out, or_3_out, or_4_out,
       or_5_out, or_6_out, or_7_out, or_8_out;

  Full_Adder full_adder_1 (.A(PC_A3), .B(PC_B3), .Ci(full_adder_2_co), .S(full_adder_1_s), .Co(PC_Co));
  and and_1 (and_1_out, nor_1_out, full_adder_1_s);
  Full_Subtractor full_subtractor_1 (
    .A(PC_B3), .B(PC_S3), .Bi(full_subtractor_2_bo), .D(full_subtractor_1_d), .Bo(PC_Bo));
  and and_2 (and_2_out, full_adder_1_s, SA_PC_A0);
  or or_1 (or_1_out, and_2_out, and_9_out);
  or or_2 (or_2_out, and_1_out, or_1_out);
  Full_Adder full_adder_2 (.A(PC_A2), .B(PC_B2), .Ci(full_adder_3_co), .S(full_adder_2_s), .Co(full_adder_2_co));
  and and_3 (and_3_out, full_adder_2_s, SA_PC_A0);
  and and_4 (and_4_out, nor_1_out, full_adder_2_s);
  or or_3 (or_3_out, and_3_out, and_11_out);
  or or_4 (or_4_out, and_4_out, or_3_out);
  Register register_1 (
    .Button(PC_Button), .Enable(PC_Enable), .Clear(PC_Clear), .IB3(or_2_out), .IB2(or_4_out), .IB1(or_5_out),
    .IB0(or_8_out), .OB3(PC_B3), .OB2(PC_B2), .OB1(PC_B1), .OB0(PC_B0));
  Full_Subtractor full_subtractor_2 (
    .A(PC_B2), .B(PC_S2), .Bi(full_subtractor_3_bo), .D(full_subtractor_2_d), .Bo(full_subtractor_2_bo));
  Full_Adder full_adder_3 (.A(PC_A1), .B(PC_B1), .Ci(full_adder_4_co), .S(full_adder_3_s), .Co(full_adder_3_co));
  and and_5 (and_5_out, nor_1_out, full_adder_3_s);
  or or_5 (or_5_out, and_5_out, or_6_out);
  Full_Subtractor full_subtractor_3 (
    .A(PC_B1), .B(PC_S1), .Bi(full_subtractor_4_bo), .D(full_subtractor_3_d), .Bo(full_subtractor_3_bo));
  and and_6 (and_6_out, full_adder_3_s, SA_PC_A0);
  or or_6 (or_6_out, and_6_out, and_10_out);
  Full_Adder full_adder_4 (.A(SA_PC_A0), .B(PC_B0), .Ci(PC_Ci), .S(full_adder_4_s), .Co(full_adder_4_co));
  and and_7 (and_7_out, nor_1_out, full_adder_4_s);
  Full_Subtractor full_subtractor_4 (
    .A(PC_B0), .B(SA_PC_S0), .Bi(Bi), .D(full_subtractor_4_d), .Bo(full_subtractor_4_bo));
  and and_8 (and_8_out, full_adder_4_s, SA_PC_A0);
  or or_7 (or_7_out, and_12_out, and_8_out);
  or or_8 (or_8_out, and_7_out, or_7_out);
  and and_9 (and_9_out, full_subtractor_1_d, SA_PC_S0);
  and and_10 (and_10_out, full_subtractor_3_d, SA_PC_S0);
  and and_11 (and_11_out, full_subtractor_2_d, SA_PC_S0);
  nor nor_1 (nor_1_out, SA_PC_A0, SA_PC_S0);
  and and_12 (and_12_out, full_subtractor_4_d, SA_PC_S0);
  Full_Adder full_adder_5 (.A(TC_A3), .B(TC_B3), .Ci(full_adder_6_co), .S(full_adder_5_s), .Co(TC_Co));
  Full_Adder full_adder_6 (.A(TC_A2), .B(TC_B2), .Ci(full_adder_7_co), .S(full_adder_6_s), .Co(full_adder_6_co));
  Register register_2 (
    .Button(TC_Button), .Enable(TC_Enable), .Clear(TC_Clear), .IB3(full_adder_5_s), .IB2(full_adder_6_s),
    .IB1(full_adder_7_s), .IB0(full_adder_8_s), .OB3(TC_B3), .OB2(TC_B2), .OB1(TC_B1), .OB0(TC_B0));
  Full_Adder full_adder_7 (.A(TC_A1), .B(TC_B1), .Ci(full_adder_8_co), .S(full_adder_7_s), .Co(full_adder_7_co));
  Full_Adder full_adder_8 (.A(SA_TC_A0), .B(TC_B0), .Ci(TC_Ci), .S(full_adder_8_s), .Co(full_adder_8_co));

  // Notes on the sheet:
  //   FA3
  //   FS3
  //   FA2
  //   FS2
  //   PC
  //   FA1
  //   FS1
  //   FA0
  //   FS0
  //   Allocation of Seat
  //   Present Count (PC) :
  //   FA3
  //   Total Participation Count (TC) :
  //   and decreasing it when a person leaves the event
  //   It keeps a track of present count by increasing it when a person enters the event,
  //   FA2
  //   It keeps a track of total participants attended to an event
  //   TC
  //   FA1
  //   FA0
endmodule

module Event_Switcher (
  input  K,
  input  A,
  input  B,
  output O
);

  wire and_1_out, and_2_out, not_1_out;

  not not_1 (not_1_out, K);
  and and_1 (and_1_out, not_1_out, A);
  and and_2 (and_2_out, K, B);
  or or_1 (O, and_1_out, and_2_out);

  // Notes on the sheet:
  //   Switcher
  //   It gives the final data of person or event 
endmodule
