// Logisim project Seat Allocator.circ as structural Verilog: 1 circuit, main circuit main
module main (
  input  SA_PC_A0,
  input  SA_TC_A0,
  input  PC_A3,
  input  PC_A2,
  input  PC_A1,
  input  PC_Ci,
  input  TC_A3,
  input  TC_A2,
  input  TC_A1,
  input  TC_Ci,
  input  TC_Button,
  input  TC_Enable,
  input  TC_Clear,
  input  PC_Button,
  input  PC_Enable,
  input  PC_Clear,
  input  SA_PC_S0,
  input  PC_S3,
  input  PC_S2,
  input  PC_S1,
  input  Bi,
  output PC_Co,
  output TC_Co,
  output TC_B3,
  output TC_B2,
  output TC_B1,
  output TC_B0,
  output PC_B3,
  output PC_B2,
  output PC_B1,
  output PC_Bo,
  output PC_B0
);

  wire and_1_out, and_2_out, and_3_out, and_4_out, and_5_out, and_6_out, and_7_out, and_8_out, and_9_out,
       and_10_out, and_11_out, and_12_out, main_1_s, main_2_d, main_3_co, main_3_s, main_5_bo, main_5_d,
       main_6_co, main_6_s, main_7_bo, main_7_d, main_8_co, main_8_s, main_9_bo, main_9_d, main_10_s,
       main_11_co, main_11_s, main_13_co, main_13_s, main_14_co, main_14_s, nor_1_out, or_1_out, or_2_out,
       or_3_out, or_4_out, or_5_out, or_6_out, or_7_out, or_8_out;

  Full_Adder_main main_1 (.A(PC_A3), .B(PC_B3), .Ci(main_3_co), .S(main_1_s), .Co(PC_Co));
  and and_1 (and_1_out, nor_1_out, main_1_s);
  Full_Subtractor_main main_2 (.A(PC_B3), .B(PC_S3), .Bi(main_5_bo), .D(main_2_d), .Bo(PC_Bo));
  and and_2 (and_2_out, main_1_s, SA_PC_A0);
  or or_1 (or_1_out, and_2_out, and_9_out);
  or or_2 (or_2_out, and_1_out, or_1_out);
  Full_Adder_main main_3 (.A(PC_A2), .B(PC_B2), .Ci(main_6_co), .S(main_3_s), .Co(main_3_co));
  and and_3 (and_3_out, nor_1_out, main_3_s);
  and and_4 (and_4_out, main_3_s, SA_PC_A0);
  or or_3 (or_3_out, and_4_out, and_11_out);
  or or_4 (or_4_out, and_3_out, or_3_out);
  Register_main main_4 (
    .Button(PC_Button), .Enable(PC_Enable), .Clear(PC_Clear), .IB3(or_2_out), .IB2(or_4_out), .IB1(or_5_out),
    .IB0(or_8_out), .OB3(PC_B3), .OB2(PC_B2), .OB1(PC_B1), .OB0(PC_B0));
  Full_Subtractor_main main_5 (.A(PC_B2), .B(PC_S2), .Bi(main_7_bo), .D(main_5_d), .Bo(main_5_bo));
  Full_Adder_main main_6 (.A(PC_A1), .B(PC_B1), .Ci(main_8_co), .S(main_6_s), .Co(main_6_co));
  and and_5 (and_5_out, nor_1_out, main_6_s);
  or or_5 (or_5_out, and_5_out, or_6_out);
  Full_Subtractor_main main_7 (.A(PC_B1), .B(PC_S1), .Bi(main_9_bo), .D(main_7_d), .Bo(main_7_bo));
  and and_6 (and_6_out, main_6_s, SA_PC_A0);
  or or_6 (or_6_out, and_6_out, and_10_out);
  Full_Adder_main main_8 (.A(SA_PC_A0), .B(PC_B0), .Ci(PC_Ci), .S(main_8_s), .Co(main_8_co));
  and and_7 (and_7_out, nor_1_out, main_8_s);
  Full_Subtractor_main main_9 (.A(PC_B0), .B(SA_PC_S0), .Bi(Bi), .D(main_9_d), .Bo(main_9_bo));
  and and_8 (and_8_out, main_8_s, SA_PC_A0);
  or or_7 (or_7_out, and_12_out, and_8_out);
  or or_8 (or_8_out, and_7_out, or_7_out);
  and and_9 (and_9_out, main_2_d, SA_PC_S0);
  and and_10 (and_10_out, main_7_d, SA_PC_S0);
  and and_11 (and_11_out, main_5_d, SA_PC_S0);
  nor nor_1 (nor_1_out, SA_PC_A0, SA_PC_S0);
  and and_12 (and_12_out, main_9_d, SA_PC_S0);
  Full_Adder_main main_10 (.A(TC_A3), .B(TC_B3), .Ci(main_11_co), .S(main_10_s), .Co(TC_Co));
  Full_Adder_main main_11 (.A(TC_A2), .B(TC_B2), .Ci(main_13_co), .S(main_11_s), .Co(main_11_co));
  Register_main main_12 (
    .Button(TC_Button), .Enable(TC_Enable), .Clear(TC_Clear), .IB3(main_10_s), .IB2(main_11_s),
    .IB1(main_13_s), .IB0(main_14_s), .OB3(TC_B3), .OB2(TC_B2), .OB1(TC_B1), .OB0(TC_B0));
  Full_Adder_main main_13 (.A(TC_A1), .B(TC_B1), .Ci(main_14_co), .S(main_13_s), .Co(main_13_co));
  Full_Adder_main main_14 (.A(SA_TC_A0), .B(TC_B0), .Ci(TC_Ci), .S(main_14_s), .Co(main_14_co));

  // Notes on the sheet:
  //   FA3
  //   FS3
  //   FA2
  //   FS2
  //   PC
  //   FA1
  //   FS1
  //   FA0
  //   FS0
  //   Allocation of Seat
  //   Present Count (PC) :
  //   FA3
  //   Total Participation Count (TC) :
  //   and decreasing it when a person leaves the event
  //   It keeps a track of present count by increasing it when a person enters the event,
  //   FA2
  //   It keeps a track of total participants attended to an event
  //   TC
  //   FA1
  //   FA0
endmodule
