// Logisim project Time Counter.circ as structural Verilog: 1 circuit, main circuit main
module main (
  input  START,
  input  Enable,
  input  Clock,
  output STOP
);

  wire FF0_q, FF0_qn, FF1_q, FF1_qn, FF2_q, FF2_qn, FF3_q, or_1_out;

  or or_1 (or_1_out, Clock, STOP);
  J_K_Flip_Flop #(.trigger("falling")) FF0 (
    .J(Enable), .clk(or_1_out), .K(Enable), .Q(FF0_q), .Qn(FF0_qn), .preset(START));  // open: en, reset
  J_K_Flip_Flop #(.trigger("falling")) FF1 (
    .J(Enable), .clk(FF0_qn), .K(Enable), .Q(FF1_q), .Qn(FF1_qn), .preset(START));  // open: en, reset
  J_K_Flip_Flop #(.trigger("falling")) FF2 (
    .J(Enable), .clk(FF1_qn), .K(Enable), .Q(FF2_q), .Qn(FF2_qn), .preset(START));  // open: en, reset
  J_K_Flip_Flop #(.trigger("falling")) FF3 (
    .J(Enable), .clk(FF2_qn), .K(Enable), .Q(FF3_q), .preset(START));  // open: Qn, en, reset
  nor nor_1 (STOP, FF3_q, FF2_q, FF1_q, FF0_q);

  // Notes on the sheet:
  //   Time Counter
  //   It indicates the remaining time of an ongoing event
endmodule
