// Logisim project Vacancy Indicator.circ as structural Verilog: 1 circuit, main circuit main
module main (
  input  P1,
  input  P0,
  input  A3,
  input  A2,
  input  A1,
  input  A0,
  input  M3,
  input  M2,
  input  M1,
  input  M0,
  output Seat_Allotment__SA,
  output VI
);

  wire O_out, X1_out, X2_out, X3_out, X4_out;

  or O (O_out, P1, P0);
  xnor X1 (X1_out, A3, M3);
  xnor X2 (X2_out, A2, M2);
  xnor X3 (X3_out, A1, M1);
  xnor X4 (X4_out, A0, M0);
  and A (VI, X1_out, X2_out, X3_out, X4_out);
  nor N (Seat_Allotment__SA, O_out, VI);

  // Notes on the sheet:
  //   Person Type
  //   Allocated Seats
  //   Maximum Capacity
  //   p
  //   w3
  //   w2
  //   w1
  //   w0
  //   VACANCY INDICATOR
  //   a
  //   It indicates the availability of seats 
endmodule
